// Logisim project ExecuteBootleg.circ as structural Verilog: 11 circuits, main circuit main
module main (
  input  [3:0] icode,
  input  [3:0] ifun,
  input  [63:0] ValA,
  input  [63:0] ValB,
  input  [63:0] ValC,
  input  clk,
  output [63:0] ValE,
  output [2:0] Cnd
);

  wire setcc_1_sccout;
  wire [1:0] alufun_1_nocodenofun;
  wire [2:0] alu_1_pcc, cc_1_cco;
  wire [63:0] ctrlogic_1_a, ctrlogic_1_b;

  CTRLogic ctrlogic_1 (.icode(icode), .valA(ValA), .valB(ValB), .valC(ValC), .A(ctrlogic_1_a), .B(ctrlogic_1_b));
  ALUfun alufun_1 (.icode(icode), .ifun(ifun), .noCodeNoFun(alufun_1_nocodenofun));
  setCC setcc_1 (.icode(icode), .SCCout(setcc_1_sccout));
  condM condm_1 (.oCC(cc_1_cco), .ifun(ifun), .cnd(Cnd));
  ALU alu_1 (.A(ctrlogic_1_a), .B(ctrlogic_1_b), .notFun(alufun_1_nocodenofun), .valE(ValE), .pCC(alu_1_pcc));
  CC cc_1 (.setCC(setcc_1_sccout), .pCC(alu_1_pcc), .clk(clk), .CCo(cc_1_cco));
endmodule

module ALU (
  input  [63:0] A,
  input  [63:0] B,
  input  [1:0] notFun,
  output [63:0] valE,
  output [2:0] pCC
);

  wire [63:0] adder_1_out, and_1_out, subtractor_1_out, xor_1_out;

  Adder #(.width(64)) adder_1 (.a(A), .b(B), .out(adder_1_out));  // open: cin, cout
  Subtractor #(.width(64)) subtractor_1 (.a(A), .b(B), .out(subtractor_1_out));  // open: bin, bout
  assign and_1_out = A & B;  // AND_Gate and_1, 64 bits wide
  assign xor_1_out = A;  // XOR_Gate xor_1, 64 bits wide XOR_Gate
  Multiplexer #(.select(2), .width(64)) multiplexer_1 (
    .in0(adder_1_out), .in1(subtractor_1_out), .in2(and_1_out), .in3(xor_1_out), .out(valE), .sel(notFun));
endmodule

module CTRLogic (
  input  [3:0] icode,
  input  [63:0] valA,
  input  [63:0] valB,
  input  [63:0] valC,
  output [63:0] A,
  output [63:0] B
);

  ALUB alub_1 (.icode(icode), .valB(valB), .B(B));
  ALUA alua_1 (.icode(icode), .valA(valA), .valC(valC), .A(A));
endmodule

module ALUA (
  input  [3:0] icode,
  input  [63:0] valA,
  input  [63:0] valC,
  output [63:0] A
);

  wire [2:0] aluahelper_1_theoutput;
  wire [63:0] adder_1_out, not_1_out, undriven;

  ALUAHelper aluahelper_1 (.icode(icode), .theOutput(aluahelper_1_theoutput));
  assign not_1_out = ~64'h8;  // NOT_Gate not_1, 64 bits wide
  Adder #(.width(64)) adder_1 (.a(not_1_out), .b({64{1'b0}}), .out(adder_1_out), .cin(1'b1));  // open: cout
  Multiplexer #(.select(3), .width(64)) multiplexer_1 (
    .in0(valA), .in1(valC), .in2(64'h8), .in3(adder_1_out), .in4(undriven), .out(A),
    .sel(aluahelper_1_theoutput));  // open: in5, in6, in7
endmodule

module ALUB (
  input  [3:0] icode,
  input  [63:0] valB,
  output [63:0] B
);

  wire [1:0] alubhelper_1_theoutput;
  wire [63:0] undriven;

  ALUBHelper alubhelper_1 (.icode(icode), .theOutput(alubhelper_1_theoutput));
  Multiplexer #(.select(2), .width(64)) multiplexer_1 (
    .in0(valB), .in1({64{1'b0}}), .in2(undriven), .out(B), .sel(alubhelper_1_theoutput));  // open: in3
endmodule

module ALUfun (
  input  [3:0] icode,
  input  [3:0] ifun,
  output [1:0] noCodeNoFun
);

  // NOT_Gate not_1 has open pins: in=icode[0], out=open
  // NOT_Gate not_2 has open pins: in=icode[1], out=open
  // NOT_Gate not_3 has open pins: in=icode[2], out=open
  // NOT_Gate not_4 has open pins: in=icode[3], out=open
  // NOT_Gate not_5 has open pins: in=ifun[0], out=open
  // NOT_Gate not_6 has open pins: in=ifun[1], out=open
  // NOT_Gate not_7 has open pins: in=ifun[2], out=open
  // NOT_Gate not_8 has open pins: in=ifun[3], out=open
endmodule

module setCC (
  input  [3:0] icode,
  output SCCout
);

  wire nand_1_out, nand_2_out, nand_3_out, nand_4_out, nand_5_out, nand_6_out, nand_7_out, nand_8_out;

  nand nand_1 (nand_1_out, 1'b1, icode[3]);
  nand nand_2 (nand_2_out, 1'b1, icode[0]);
  nand nand_3 (nand_3_out, nand_1_out, icode[1]);
  nand nand_4 (nand_4_out, nand_1_out, icode[2]);
  nand nand_5 (nand_5_out, nand_3_out, nand_3_out);
  nand nand_6 (nand_6_out, nand_4_out, nand_4_out);
  nand nand_7 (nand_7_out, nand_5_out, nand_2_out);
  nand nand_8 (nand_8_out, nand_6_out, icode[1]);
  nand nand_9 (SCCout, nand_7_out, nand_8_out);
endmodule

module CC (
  input  setCC,
  input  [2:0] pCC,
  input  clk,
  output [2:0] CCo
);

  Register #(.width(3)) register_1 (.D(pCC), .en(setCC), .clk(clk), .Q(CCo));  // open: clr
endmodule

module condM (
  input  [2:0] oCC,
  input  [3:0] ifun,
  output [2:0] cnd
);
endmodule

module ALUAHelper (
  input  [3:0] icode,
  output [2:0] theOutput
);
endmodule

module ALUBHelper (
  input  [3:0] icode,
  output [1:0] theOutput
);
endmodule
