// Logisim project Lab6.circ as structural Verilog: 16 circuits, main circuit main
module main (
  input  [7:0] PC
);

  wire clock_1_out, fetch_1_complete, undriven_2;
  wire [3:0] fetch_1_icode, fetch_1_ifun, fetch_1_ra, fetch_1_rb;
  wire [7:0] fetch_1_valp, undriven;
  wire [63:0] decode_1_vala, fetch_1_valc, memory_1_valm;

  Clock clock_1 (.out(clock_1_out));
  Fetch fetch_1 (
    .PC(PC), .clk(clock_1_out), .iCode(fetch_1_icode), .iFun(fetch_1_ifun), .rA(fetch_1_ra), .rB(fetch_1_rb),
    .valC(fetch_1_valc), .valP(fetch_1_valp), .Complete(fetch_1_complete));  // open: Reset
  Decode decode_1 (
    .iCode(fetch_1_icode), .clk(clock_1_out), .valM(memory_1_valm), .valA(decode_1_vala));  // open: rA, rB, ME_Enable, valE, valB
  Memory memory_1 (
    .icode(fetch_1_icode), .valE(undriven), .valA(decode_1_vala), .valP(fetch_1_valp), .clk(clock_1_out),
    .valM(memory_1_valm));
  WriteBack writeback_1 (.iCode(fetch_1_icode), .rA(fetch_1_ra), .rB(fetch_1_rb));  // open: dstE, dstM
  PCUpdate pcupdate_1 (
    .iCode(fetch_1_icode), .valP(fetch_1_valp), .valE(undriven), .cnd(undriven_2), .newPC(PC));  // open: valC
endmodule

module Decode (
  input  [3:0] iCode,
  input  [3:0] rA,
  input  [3:0] rB,
  input  clk,
  input  ME_Enable,
  input  [63:0] valM,
  input  [63:0] valE,
  output [63:0] valA,
  output [63:0] valB
);

  wire [3:0] dste_1_out_3, dstm_1_out_3, srca_1_out_3, srcb_1_out_3;

  dstM dstm_1 (.iCode(iCode), .rA(rA), .out_3(dstm_1_out_3));
  dstE dste_1 (.iCode(iCode), .rB(rB), .out_3(dste_1_out_3));
  srcA srca_1 (.iCode(iCode), .rA(rA), .out_3(srca_1_out_3));
  srcB srcb_1 (.iCode(iCode), .rB(rB), .out_3(srcb_1_out_3));
  Register_File register_file_1 (
    .valM(valM), .valE(valE), .dstM(dstm_1_out_3), .dstE(dste_1_out_3), .ME(ME_Enable), .srcA(srca_1_out_3),
    .srcB(srcb_1_out_3), .clk(clk), .valA(valA), .valB(valB));
endmodule

module Register_File (
  input  [63:0] valM,
  input  [63:0] valE,
  input  [3:0] dstM,
  input  [3:0] dstE,
  input  ME,
  input  [3:0] srcA,
  input  [3:0] srcB,
  input  clk,
  output [63:0] valA,
  output [63:0] valB
);

  wire demultiplexer_2_out0, demultiplexer_2_out1, demultiplexer_2_out2, demultiplexer_2_out3,
       demultiplexer_2_out4, demultiplexer_2_out5, demultiplexer_2_out6, demultiplexer_2_out7,
       demultiplexer_2_out8, demultiplexer_2_out9, demultiplexer_2_out10, demultiplexer_2_out11,
       demultiplexer_2_out12, demultiplexer_2_out13, demultiplexer_2_out14;
  wire [3:0] multiplexer_2_out;
  wire [63:0] demultiplexer_1_out0, demultiplexer_1_out1, demultiplexer_1_out2, demultiplexer_1_out3,
       demultiplexer_1_out4, demultiplexer_1_out5, demultiplexer_1_out6, demultiplexer_1_out7,
       demultiplexer_1_out8, demultiplexer_1_out9, demultiplexer_1_out10, demultiplexer_1_out11,
       demultiplexer_1_out12, demultiplexer_1_out13, demultiplexer_1_out14, multiplexer_1_out, r8_8_q,
       r9_9_q, r10_A_q, r11_B_q, r12_C_q, r13_D_q, r14_E_q, rax_0_q, rbp_5_q, rbx_3_q, rcx_1_q, rdi_7_q,
       rdx_2_q, rsi_6_q, rsp_4_q;

  Multiplexer #(.width(64)) multiplexer_1 (.in0(valM), .in1(valE), .out(multiplexer_1_out), .sel(ME));
  Demultiplexer #(.select(4), .width(64)) demultiplexer_1 (
    .out0(demultiplexer_1_out0), .out1(demultiplexer_1_out1), .out2(demultiplexer_1_out2),
    .out3(demultiplexer_1_out3), .out4(demultiplexer_1_out4), .out5(demultiplexer_1_out5),
    .out6(demultiplexer_1_out6), .out7(demultiplexer_1_out7), .out8(demultiplexer_1_out8),
    .out9(demultiplexer_1_out9), .out10(demultiplexer_1_out10), .out11(demultiplexer_1_out11),
    .out12(demultiplexer_1_out12), .out13(demultiplexer_1_out13), .out14(demultiplexer_1_out14),
    .in(multiplexer_1_out), .sel(multiplexer_2_out));  // open: out15
  Multiplexer #(.width(4)) multiplexer_2 (.in0(dstM), .in1(dstE), .out(multiplexer_2_out), .sel(ME));
  Demultiplexer #(.select(4)) demultiplexer_2 (
    .out0(demultiplexer_2_out0), .out1(demultiplexer_2_out1), .out2(demultiplexer_2_out2),
    .out3(demultiplexer_2_out3), .out4(demultiplexer_2_out4), .out5(demultiplexer_2_out5),
    .out6(demultiplexer_2_out6), .out7(demultiplexer_2_out7), .out8(demultiplexer_2_out8),
    .out9(demultiplexer_2_out9), .out10(demultiplexer_2_out10), .out11(demultiplexer_2_out11),
    .out12(demultiplexer_2_out12), .out13(demultiplexer_2_out13), .out14(demultiplexer_2_out14), .in(1'b1),
    .sel(multiplexer_2_out));  // open: out15
  Register #(.width(64)) rax_0 (
    .D(demultiplexer_1_out0), .en(demultiplexer_2_out0), .clk(clk), .Q(rax_0_q));  // open: clr
  Register #(.width(64)) rcx_1 (
    .D(demultiplexer_1_out1), .en(demultiplexer_2_out1), .clk(clk), .Q(rcx_1_q));  // open: clr
  Register #(.width(64)) rdx_2 (
    .D(demultiplexer_1_out2), .en(demultiplexer_2_out2), .clk(clk), .Q(rdx_2_q));  // open: clr
  Register #(.width(64)) rbx_3 (
    .D(demultiplexer_1_out3), .en(demultiplexer_2_out3), .clk(clk), .Q(rbx_3_q));  // open: clr
  Register #(.width(64)) rsp_4 (
    .D(demultiplexer_1_out4), .en(demultiplexer_2_out4), .clk(clk), .Q(rsp_4_q));  // open: clr
  Register #(.width(64)) rbp_5 (
    .D(demultiplexer_1_out5), .en(demultiplexer_2_out5), .clk(clk), .Q(rbp_5_q));  // open: clr
  Register #(.width(64)) rsi_6 (
    .D(demultiplexer_1_out6), .en(demultiplexer_2_out6), .clk(clk), .Q(rsi_6_q));  // open: clr
  Register #(.width(64)) rdi_7 (
    .D(demultiplexer_1_out7), .en(demultiplexer_2_out7), .clk(clk), .Q(rdi_7_q));  // open: clr
  Register #(.width(64)) r8_8 (
    .D(demultiplexer_1_out8), .en(demultiplexer_2_out8), .clk(clk), .Q(r8_8_q));  // open: clr
  Register #(.width(64)) r9_9 (
    .D(demultiplexer_1_out9), .en(demultiplexer_2_out9), .clk(clk), .Q(r9_9_q));  // open: clr
  Register #(.width(64)) r10_A (
    .D(demultiplexer_1_out10), .en(demultiplexer_2_out10), .clk(clk), .Q(r10_A_q));  // open: clr
  Register #(.width(64)) r11_B (
    .D(demultiplexer_1_out11), .en(demultiplexer_2_out11), .clk(clk), .Q(r11_B_q));  // open: clr
  Register #(.width(64)) r12_C (
    .D(demultiplexer_1_out12), .en(demultiplexer_2_out12), .clk(clk), .Q(r12_C_q));  // open: clr
  Register #(.width(64)) r13_D (
    .D(demultiplexer_1_out13), .en(demultiplexer_2_out13), .clk(clk), .Q(r13_D_q));  // open: clr
  Register #(.width(64)) r14_E (
    .D(demultiplexer_1_out14), .en(demultiplexer_2_out14), .clk(clk), .Q(r14_E_q));  // open: clr
  Multiplexer #(.select(4), .width(64)) multiplexer_3 (
    .in0(rax_0_q), .in1(rcx_1_q), .in2(rdx_2_q), .in3(rbx_3_q), .in4(rsp_4_q), .in5(rbp_5_q), .in6(rsi_6_q),
    .in7(rdi_7_q), .in8(r8_8_q), .in9(r9_9_q), .in10(r10_A_q), .in11(r11_B_q), .in12(r12_C_q),
    .in13(r13_D_q), .in14(r14_E_q), .out(valA), .sel(srcA));  // open: in15
  Multiplexer #(.select(4), .width(64)) multiplexer_4 (
    .in0(rax_0_q), .in1(rcx_1_q), .in2(rdx_2_q), .in3(rbx_3_q), .in4(rsp_4_q), .in5(rbp_5_q), .in6(rsi_6_q),
    .in7(rdi_7_q), .in8(r8_8_q), .in9(r9_9_q), .in10(r10_A_q), .in11(r11_B_q), .in12(r12_C_q),
    .in13(r13_D_q), .in14(r14_E_q), .out(valB), .sel(srcB));  // open: in15
endmodule

module dstE (
  input  [3:0] iCode,
  input  [3:0] rB,
  output [3:0] out_3
);

  wire decoder_1_out2, decoder_1_out3, decoder_1_out4, decoder_1_out6, or_1_out;

  Decoder #(.select(4)) decoder_1 (
    .out2(decoder_1_out2), .out3(decoder_1_out3), .out4(decoder_1_out4), .out6(decoder_1_out6), .sel(iCode));  // open: out0, out1, out5, out7, out8, out9, out10, out11, out12, out13, out14, out15, en
  Multiplexer #(.width(4)) multiplexer_1 (.in0(4'b1111), .in1(rB), .out(out_3), .sel(or_1_out));
  or or_1 (or_1_out, decoder_1_out2, decoder_1_out3, decoder_1_out4, decoder_1_out6);
endmodule

module dstM (
  input  [3:0] iCode,
  input  [3:0] rA,
  output [3:0] out_3
);

  wire decoder_1_out5, decoder_1_out11, or_1_out;

  Decoder #(.select(4)) decoder_1 (
    .out5(decoder_1_out5), .out11(decoder_1_out11), .sel(iCode));  // open: out0, out1, out2, out3, out4, out6, out7, out8, out9, out10, out12, out13, out14, out15, en
  or or_1 (or_1_out, decoder_1_out5, decoder_1_out11);
  Multiplexer #(.width(4)) multiplexer_1 (.in0(4'b1111), .in1(rA), .out(out_3), .sel(or_1_out));
endmodule

module srcA (
  input  [3:0] iCode,
  input  [3:0] rA,
  output [3:0] out_3
);

  wire decoder_1_out2, decoder_1_out4, decoder_1_out6, decoder_1_out10, or_1_out;

  Decoder #(.select(4)) decoder_1 (
    .out2(decoder_1_out2), .out4(decoder_1_out4), .out6(decoder_1_out6), .out10(decoder_1_out10), .sel(iCode));  // open: out0, out1, out3, out5, out7, out8, out9, out11, out12, out13, out14, out15, en
  or or_1 (or_1_out, decoder_1_out2, decoder_1_out4, decoder_1_out6, decoder_1_out10);
  Multiplexer #(.width(4)) multiplexer_1 (.in0(4'b1111), .in1(rA), .out(out_3), .sel(or_1_out));
endmodule

module srcB (
  input  [3:0] iCode,
  input  [3:0] rB,
  output [3:0] out_3
);

  wire decoder_1_out5, or_1_out;

  Decoder #(.select(4)) decoder_1 (
    .out5(decoder_1_out5), .sel(iCode));  // open: out0, out1, out2, out3, out4, out6, out7, out8, out9, out10, out11, out12, out13, out14, out15, en
  Multiplexer #(.width(4)) multiplexer_1 (.in0(4'b1111), .in1(rB), .out(out_3), .sel(or_1_out));
  buf or_1 (or_1_out, decoder_1_out5);  // OR_Gate
endmodule

module Memory (
  input  [3:0] icode,
  input  [7:0] valE,
  input  [63:0] valA,
  input  [7:0] valP,
  input  clk,
  output [63:0] valM
);

  wire memhelper_1_addrenable, memhelper_1_datenable, memhelper_1_oenable, memhelper_1_wenable,
       memregenable_1_e0, memregenable_1_e1, memregenable_1_e2, memregenable_1_e3, memregenable_1_e4,
       memregenable_1_e5, memregenable_1_e6, memregenable_1_e7, not_1_out, undriven;
  wire [2:0] counter_1_q;
  wire [7:0] adder_1_out, controlled_buffer_1_out, controlled_buffer_2_out, multiplexer_1_out,
       multiplexer_2_out, multiplexer_3_out, ram_1_dout, register_1_q, register_2_q, register_3_q,
       register_4_q, register_5_q, register_6_q, register_7_q, register_8_q;

  Counter #(.max('h7), .width(3)) counter_1 (.clk(clk), .Q(counter_1_q));  // open: clr, load, up, count, D, carry
  memHelper memhelper_1 (
    .icode(icode), .oEnable(memhelper_1_oenable), .wEnable(memhelper_1_wenable),
    .addrEnable(memhelper_1_addrenable), .datEnable(memhelper_1_datenable));
  Multiplexer #(.width(8)) multiplexer_1 (
    .in0(valE), .in1(valA[63:56]), .out(multiplexer_1_out), .sel(memhelper_1_addrenable));
  Adder adder_1 (.a(multiplexer_1_out), .b({{5{1'b0}}, counter_1_q}), .out(adder_1_out));  // open: cin, cout
  Multiplexer #(.select(3), .width(8)) multiplexer_2 (
    .in0(valA[7:0]), .in1(valA[15:8]), .in2(valA[23:16]), .in3(valA[31:24]), .in4(valA[39:32]),
    .in5(valA[47:40]), .in6(valA[55:48]), .in7(valA[63:56]), .out(multiplexer_2_out));  // open: sel
  assign controlled_buffer_1_out = memhelper_1_wenable ? multiplexer_2_out : 8'bz;  // Controlled_Buffer controlled_buffer_1
  not not_1 (not_1_out, memhelper_1_wenable);
  RAM ram_1 (
    .addr(adder_1_out), .we(memhelper_1_wenable), .oe(not_1_out), .clk(clk), .din(multiplexer_3_out),
    .dout(ram_1_dout));
  Multiplexer #(.width(8)) multiplexer_3 (
    .in0(controlled_buffer_1_out), .in1(valP), .out(multiplexer_3_out), .sel(memhelper_1_datenable));
  assign controlled_buffer_2_out = not_1_out ? ram_1_dout : 8'bz;  // Controlled_Buffer controlled_buffer_2
  MemRegEnable memregenable_1 (
    .cntr(counter_1_q), .enable(not_1_out), .E0(memregenable_1_e0), .E1(memregenable_1_e1),
    .E2(memregenable_1_e2), .E3(memregenable_1_e3), .E4(memregenable_1_e4), .E5(memregenable_1_e5),
    .E6(memregenable_1_e6), .E7(memregenable_1_e7));
  Register register_1 (
    .D(controlled_buffer_2_out), .en(memregenable_1_e0), .clk(clk), .Q(register_1_q), .clr(undriven));
  Register register_2 (
    .D(controlled_buffer_2_out), .en(memregenable_1_e1), .clk(clk), .Q(register_2_q), .clr(undriven));
  Register register_3 (
    .D(controlled_buffer_2_out), .en(memregenable_1_e2), .clk(clk), .Q(register_3_q), .clr(undriven));
  Register register_4 (
    .D(controlled_buffer_2_out), .en(memregenable_1_e3), .clk(clk), .Q(register_4_q), .clr(undriven));
  Register register_5 (
    .D(controlled_buffer_2_out), .en(memregenable_1_e4), .clk(clk), .Q(register_5_q), .clr(undriven));
  Register register_6 (
    .D(controlled_buffer_2_out), .en(memregenable_1_e5), .clk(clk), .Q(register_6_q), .clr(undriven));
  Register register_7 (
    .D(controlled_buffer_2_out), .en(memregenable_1_e6), .clk(clk), .Q(register_7_q), .clr(undriven));
  Register register_8 (
    .D(controlled_buffer_2_out), .en(memregenable_1_e7), .clk(clk), .Q(register_8_q), .clr(undriven));
  assign valM = memhelper_1_oenable ? {register_8_q, register_7_q, register_6_q, register_5_q, register_4_q, register_3_q, register_2_q, register_1_q} : 64'bz;  // Controlled_Buffer controlled_buffer_3
endmodule

module memHelper (
  input  [3:0] icode,
  output oEnable,
  output wEnable,
  output addrEnable,
  output datEnable
);

  wire and_1_out, and_2_out, and_3_out, and_4_out, not_1_out, not_2_out, not_3_out, not_4_out;

  not not_1 (not_1_out, icode[3]);
  not not_2 (not_2_out, icode[2]);
  not not_3 (not_3_out, icode[1]);
  not not_4 (not_4_out, icode[0]);
  and and_1 (and_1_out, not_1_out, icode[2], not_3_out, icode[0]);
  and and_2 (and_2_out, icode[3], not_2_out, icode[0]);
  and and_3 (and_3_out, not_1_out, icode[2], not_3_out, not_4_out);
  and and_4 (and_4_out, icode[3], not_2_out, not_4_out);
  and and_5 (addrEnable, icode[3], not_2_out, icode[0]);
  and and_6 (datEnable, icode[3], not_2_out, not_3_out, not_4_out);
  or or_1 (oEnable, and_1_out, and_2_out);
  or or_2 (wEnable, and_3_out, and_4_out);
endmodule

module MemRegEnable (
  input  [2:0] cntr,
  input  enable,
  output E0,
  output E1,
  output E2,
  output E3,
  output E4,
  output E5,
  output E6,
  output E7
);

  wire not_1_out, not_2_out, not_3_out;

  not not_1 (not_1_out, cntr[2]);
  not not_2 (not_2_out, cntr[1]);
  not not_3 (not_3_out, cntr[0]);
  and and_1 (E0, not_1_out, not_2_out, cntr[0], enable);
  and and_2 (E1, not_1_out, cntr[1], not_3_out, enable);
  and and_3 (E2, not_1_out, cntr[1], cntr[0], enable);
  and and_4 (E3, cntr[2], not_2_out, not_3_out, enable);
  and and_5 (E4, cntr[2], not_2_out, cntr[0], enable);
  and and_6 (E5, cntr[2], cntr[1], not_3_out, enable);
  and and_7 (E6, cntr[2], cntr[1], cntr[0], enable);
  and and_8 (E7, not_1_out, not_2_out, not_3_out, enable);
endmodule

module Fetch (
  input  [7:0] PC,
  input  clk,
  input  Reset,
  output [3:0] iCode,
  output [3:0] iFun,
  output [3:0] rA,
  output [3:0] rB,
  output [63:0] valC,
  output [7:0] valP,
  output Complete
);

  wire fetchregenable_1_e0, fetchregenable_1_e1, fetchregenable_1_e2, fetchregenable_1_e3,
       fetchregenable_1_e4, fetchregenable_1_e5, fetchregenable_1_e6, fetchregenable_1_e7,
       fetchregenable_1_e8, fetchregenable_1_e9;
  wire [7:0] adder_1_out, adder_2_out, counter_1_q, fetchvalp_1_valp, register_1_q, register_2_q,
       register_3_q, register_4_q, register_5_q, register_6_q, register_7_q, register_8_q, register_14_q,
       rom_1_data;

  Adder adder_1 (.a(PC), .b(counter_1_q), .out(adder_1_out));  // open: cin, cout
  ROM rom_1 (.addr(adder_1_out), .data(rom_1_data));
  FetchRegEnable fetchregenable_1 (
    .cntr(counter_1_q), .E0(fetchregenable_1_e0), .E1(fetchregenable_1_e1), .E2(fetchregenable_1_e2),
    .E3(fetchregenable_1_e3), .E4(fetchregenable_1_e4), .E5(fetchregenable_1_e5), .E6(fetchregenable_1_e6),
    .E7(fetchregenable_1_e7), .E8(fetchregenable_1_e8), .E9(fetchregenable_1_e9));
  Register register_1 (.D(rom_1_data), .en(fetchregenable_1_e2), .clk(clk), .Q(register_1_q), .clr(Reset));
  Register register_2 (.D(rom_1_data), .en(fetchregenable_1_e3), .clk(clk), .Q(register_2_q), .clr(Reset));
  Register register_3 (.D(rom_1_data), .en(fetchregenable_1_e4), .clk(clk), .Q(register_3_q), .clr(Reset));
  Register register_4 (.D(rom_1_data), .en(fetchregenable_1_e5), .clk(clk), .Q(register_4_q), .clr(Reset));
  Register register_5 (.D(rom_1_data), .en(fetchregenable_1_e6), .clk(clk), .Q(register_5_q), .clr(Reset));
  Register register_6 (.D(rom_1_data), .en(fetchregenable_1_e7), .clk(clk), .Q(register_6_q), .clr(Reset));
  Register register_7 (.D(rom_1_data), .en(fetchregenable_1_e8), .clk(clk), .Q(register_7_q), .clr(Reset));
  Register register_8 (.D(rom_1_data), .en(fetchregenable_1_e9), .clk(clk), .Q(register_8_q), .clr(Reset));
  FetchValP fetchvalp_1 (.iCode(rom_1_data[7:4]), .valP(fetchvalp_1_valp));
  Counter #(.max('hf)) counter_1 (.clr(Complete), .clk(clk), .Q(counter_1_q));  // open: load, up, count, D, carry
  Register #(.width(4)) register_9 (.D(rom_1_data[7:4]), .en(fetchregenable_1_e0), .clk(clk), .Q(iCode), .clr(Reset));
  Register #(.width(4)) register_10 (.D(rom_1_data[3:0]), .en(fetchregenable_1_e0), .clk(clk), .Q(iFun), .clr(Reset));
  Register #(.width(4)) register_11 (.D(rom_1_data[7:4]), .en(fetchregenable_1_e1), .clk(clk), .Q(rA), .clr(Reset));
  Register #(.width(4)) register_12 (.D(rom_1_data[3:0]), .en(fetchregenable_1_e1), .clk(clk), .Q(rB), .clr(Reset));
  Register #(.width(64)) register_13 (
    .D({register_8_q, register_7_q, register_6_q, register_5_q, register_4_q, register_3_q, register_2_q, register_1_q}),
    .en(1'b1), .clk(clk), .Q(valC), .clr(Reset));
  Register register_14 (.D(fetchvalp_1_valp), .en(fetchregenable_1_e0), .clk(clk), .Q(register_14_q), .clr(Reset));
  Adder adder_2 (.a(PC), .b(register_14_q), .out(adder_2_out));  // open: cin, cout
  Comparator #(.mode("unsigned")) comparator_1 (.a(register_14_q), .b(counter_1_q), .eq(Complete));  // open: gt, lt
  Register register_15 (.D(adder_2_out), .clk(clk), .Q(valP), .clr(Reset));  // open: en

  // Notes on the sheet:
  //   contents of rom_1 (hex, n*v repeats v):
  //   30 f8 8 13*0 30 f9 1 13*0 63 15*0 30 f6 5 13*0 62 66 14*0 70 2f 30*0 60 80 14*0 61 96 30*0 74 2b
endmodule

module FetchRegEnable (
  input  [7:0] cntr,
  output E0,
  output E1,
  output E2,
  output E3,
  output E4,
  output E5,
  output E6,
  output E7,
  output E8,
  output E9
);

  wire not_1_out, not_2_out, not_3_out, not_4_out;

  not not_1 (not_1_out, cntr[3]);
  not not_2 (not_2_out, cntr[2]);
  not not_3 (not_3_out, cntr[1]);
  not not_4 (not_4_out, cntr[0]);
  and and_1 (E0, not_1_out, not_2_out, not_3_out, not_4_out);
  and and_2 (E1, not_1_out, not_2_out, not_3_out, cntr[0]);
  and and_3 (E2, not_1_out, not_2_out, cntr[1], not_4_out);
  and and_4 (E3, not_1_out, not_2_out, cntr[1], cntr[0]);
  and and_5 (E4, not_1_out, cntr[2], not_3_out, not_4_out);
  and and_6 (E5, not_1_out, cntr[2], not_3_out, cntr[0]);
  and and_7 (E6, not_1_out, cntr[2], cntr[1], not_4_out);
  and and_8 (E7, not_1_out, cntr[2], cntr[1], cntr[0]);
  and and_9 (E8, cntr[3], not_2_out, not_3_out, not_4_out);
  and and_10 (E9, cntr[3], not_2_out, not_3_out, cntr[0]);
endmodule

module FetchValP (
  input  [3:0] iCode,
  output [7:0] valP
);

  wire and_1_out, and_2_out, and_3_out, and_4_out, and_5_out, and_6_out, and_7_out, and_8_out, not_1_out,
       not_2_out, not_3_out, not_4_out;

  not not_1 (not_1_out, iCode[3]);
  not not_2 (not_2_out, iCode[2]);
  not not_3 (not_3_out, iCode[1]);
  not not_4 (not_4_out, iCode[0]);
  and and_1 (and_1_out, not_1_out, iCode[1], iCode[0]);
  and and_2 (and_2_out, not_1_out, iCode[2], not_3_out);
  and and_3 (and_3_out, iCode[3], not_2_out, not_3_out, not_4_out);
  and and_4 (and_4_out, not_2_out, iCode[1]);
  and and_5 (and_5_out, not_1_out, iCode[2], not_3_out);
  and and_6 (and_6_out, not_1_out, iCode[1], not_4_out);
  and and_7 (and_7_out, not_2_out, not_3_out);
  and and_8 (and_8_out, not_1_out, iCode[2], iCode[1], iCode[0]);
  or or_1 (valP[3], and_1_out, and_2_out, and_3_out);
  or or_2 (valP[1], and_4_out, and_5_out, and_6_out);
  or or_3 (valP[0], and_7_out, and_8_out);

  assign {valP[7:4], valP[2]} = {5{1'b0}};
endmodule

module WriteBack (
  input  [3:0] iCode,
  input  [3:0] rA,
  input  [3:0] rB,
  output [3:0] dstE,
  output [3:0] dstM
);

  Multiplexer #(.select(4), .width(4)) multiplexer_1 (
    .in2(rB), .in3(rB), .in5(rA), .in6(rB), .in8(4'b0100), .in9(4'b0100), .in10(4'b0100), .in11(4'b0100),
    .out(dstE), .sel(iCode));  // open: in0, in1, in4, in7, in12, in13, in14, in15

  assign dstM = dstE;
endmodule

module WBDecoder (
  input  [3:0] iCode,
  output O_0,
  output O_1,
  output O_2,
  output O_3,
  output O_4,
  output O_5,
  output O_6,
  output O_7,
  output O_8,
  output O_9,
  output O_A,
  output O_B,
  output O_C,
  output O_D,
  output O_E,
  output O_F
);

  wire not_1_out, not_2_out, not_3_out, not_4_out;

  not not_1 (not_1_out, iCode[3]);
  not not_2 (not_2_out, iCode[2]);
  not not_3 (not_3_out, iCode[1]);
  not not_4 (not_4_out, iCode[0]);
  and and_1 (O_0, not_1_out, not_2_out, not_3_out, not_4_out);
  and and_2 (O_1, not_1_out, not_2_out, not_3_out, iCode[0]);
  and and_3 (O_2, not_1_out, not_2_out, iCode[1], not_4_out);
  and and_4 (O_3, not_1_out, not_2_out, iCode[1], iCode[0]);
  and and_5 (O_4, not_1_out, iCode[2], not_3_out, not_4_out);
  and and_6 (O_5, not_1_out, iCode[2], not_3_out, iCode[0]);
  and and_7 (O_6, not_1_out, iCode[2], iCode[1], not_4_out);
  and and_8 (O_7, not_1_out, iCode[2], iCode[1], iCode[0]);
  and and_9 (O_8, iCode[3], not_2_out, not_3_out, not_4_out);
  and and_10 (O_9, iCode[3], not_2_out, not_3_out, iCode[0]);
  and and_11 (O_A, iCode[3], not_2_out, iCode[1], not_4_out);
  and and_12 (O_B, iCode[3], not_2_out, iCode[1], iCode[0]);
  and and_13 (O_C, iCode[3], iCode[2], not_3_out, not_4_out);
  and and_14 (O_D, iCode[3], iCode[2], not_3_out, iCode[0]);
  and and_15 (O_E, iCode[3], iCode[2], iCode[1], not_4_out);
  and and_16 (O_F, iCode[3], iCode[2], iCode[1], iCode[0]);
endmodule

module PCUpdate (
  input  [3:0] iCode,
  input  [7:0] valP,
  input  [7:0] valE,
  input  cnd,
  input  [63:0] valC,
  output [7:0] newPC
);

  wire [7:0] multiplexer_1_out;

  Multiplexer #(.width(8)) multiplexer_1 (.in0(valP), .in1(valC[7:0]), .out(multiplexer_1_out), .sel(cnd));
  Multiplexer #(.select(4), .width(8)) multiplexer_2 (
    .in0(valP), .in1(valP), .in2(valP), .in3(valP), .in4(valP), .in5(valP), .in6(valP), .in7(valP),
    .in8(multiplexer_1_out), .in9(valE), .in10(valE), .in11(valP), .in12(valP), .out(newPC), .sel(iCode));  // open: in13, in14, in15
endmodule
